# Fritzing sketch Component Diagram (saved by Fritzing 1.0.2b)

parts:
  Mod1 = Raspberry Pi 4B  # not connected
  S1 = H-Bridge with L298N
  DC_PUMP = DC Motor [voltage_(max)=6V voltage_(min)=3V]
  Part1 = Arduino Uno (Rev3)
  M2 = bb-usb-cable [package=THT]  # not connected
  U2D2 = Arduino Nano (Rev3.0)  # not connected
  M3 = bb-usb-cable [package=THT]  # not connected
  J1 = Basic Servo  # not connected
  J2 = Basic Servo  # not connected
  DYNAMIXELS = Basic Servo  # not connected
  U1 = LIPO-110mAh [package=lipo-110]
  U2 = LIPO-110mAh [package=lipo-110]
  VOLTAGE_REGULATOR = Mini-360 DC-DC Buck converter [package=THT]

nets:
  N1: S1.12V, VOLTAGE_REGULATOR.OUT+
  GND: S1.GND, Part1.GND, VOLTAGE_REGULATOR.OUT-
  N2: S1.IN1, Part1.D6_PWM
  N3: S1.IN2, Part1.D5_PWM
  N4: S1.M1-01, DC_PUMP.pin_2
  N5: S1.M1-02, DC_PUMP.pin_1
  N6: U1.+, VOLTAGE_REGULATOR.IN+
  N7: U1.-, U2.+
  N8: U2.-, VOLTAGE_REGULATOR.IN-

custom parts:
  H-Bridge with L298N: h-bridge
  bb-usb-cable: Breadboard only, no connectors USB cable for the Raspberry PIs.
  Mini-360 DC-DC Buck converter: Mini-360 DC-DC Buck converter. Tiny buck step down voltage converter, input voltage 4.75 to 23V output 1 to 17V adjustable. Available from ebay and the like.
